# Fritzing sketch Edge Detection Schematic (saved by Fritzing 0.9.3b)
breadboards: 1

parts:
  U2 = LM124-324 Quad Opamp [package="DIP (Dual Inline)"]
  R2 = Resistor [tolerance=±5% resistance=1.5k package=THT]
  R1 = Resistor [tolerance=±5% resistance=390 package=THT]
  LM317 = Voltage Regulator - Variable [package="TO220 [THT]"]
  INPUT = Screw terminal - 2 pins [package=THT]
  Buzzer = Piezo Speaker
  Switch = Round Pushbutton
  R3 = Resistor [tolerance=±5% resistance=10 package=THT]
  R4 = Resistor [tolerance=±5% resistance=2.2k package=THT]
  IC1 = IC, DIP package, 8 pins [chip_label="Collar Circuit"]
  JP1 = Header 3 [package=screwterminal-3.5mm-3_lock.007s]
  Connector = Header 3 [package=screwterminal-3.5mm-3_lock.007s]
  To_Arduino_Digital_Pin = Screw terminal - 2 pins [package=THT]

nets:
  N1: U2.1OUT, To_Arduino_Digital_Pin.pin1
  N2: U2.1IN-, Connector.3
  N3: U2.1IN+, R4.Pin_0
  N4: U2.VCC+, R1.Pin_0, LM317.OUT, R3.Pin_1, Connector.1
  GND: U2.VCC-, R2.Pin_1, INPUT.pin1, R4.Pin_1, Connector.2
  N5: R2.Pin_0, R1.Pin_1, LM317.ADJ
  N6: LM317.IN, INPUT.pin2
  N7: Buzzer.pin1, IC1.pin8
  N8: Buzzer.pin2, Switch.leg1
  N9: Switch.leg0, IC1.pin7
  N10: IC1.pin1, JP1.3
  N11: IC1.pin2, IC1.pin3, JP1.2
  N12: IC1.pin4, JP1.1
