# Fritzing sketch Final Schematic (saved by Fritzing 0.9.3b)
breadboards: 1

parts:
  U2 = LM124-324 Quad Opamp [package="DIP (Dual Inline)"]
  R2 = Resistor [tolerance=±5% resistance=1.5k package=THT]
  R1 = Resistor [tolerance=±5% resistance=390 package=THT]
  LM317 = Voltage Regulator - Variable [package="TO220 [THT]"]
  INPUT = Screw terminal - 2 pins [package=THT]
  Buzzer = Piezo Speaker
  Switch = Round Pushbutton
  R3 = Resistor [tolerance=±5% resistance=10 package=THT]
  R4 = Resistor [tolerance=±5% resistance=2.2k package=THT]
  IC1 = IC, DIP package, 8 pins [chip_label="Collar Circuit"]
  JP1 = Header 3 [package=screwterminal-3.5mm-3_lock.007s]
  Connector = Header 3 [package=screwterminal-3.5mm-3_lock.007s]
  To_Arduino_Digital_Pin = Screw terminal - 2 pins [package=THT]
  Contactor = RELAY [package=relay-g5q]
  Part1 = Arduino Mega ADK (Rev3)
  Battery_1 = Battery Holders [part_number="12 Vdc" package=battery]
  Battery_2 = Battery Holders [part_number="12 Vdc" package=battery]
  Emergency_Stop_Switch_(NC) = SWITCH-MOMENTARY-2 [package=tactile_switch_smd-2]
  Digital_Relay_Module = IC, DIP package, 6 pins [chip_label="Relay Module"]
  12v_Regulator = Voltage Regulator [package=to220-igo]
  5v_Regulator = Voltage Regulator [package=78xxl]
  U3 = XBEE-1 [package=xbee-1_lock]
  Motor_1 = DC Motor
  Motor_2 = DC Motor
  Brake_1 = Inductor [package="1206 [SMD]"]
  Brake_2 = Inductor [package="1206 [SMD]"]
  INPUT1 = Screw terminal - 2 pins [package=THT]
  Switch_2 = Pushbutton [package=THT]
  To_Arduino_Digital_Pin1 = Screw terminal - 2 pins [package=THT]
  Sabertooth_2X60 = IC, DIP package, 10 pins [chip_label=2x60]
  Ultrasonic_Sensor_1 = IC, SIP package, 4 pins [chip_label=Ultrasonic]

nets:
  N1: U2.1OUT, To_Arduino_Digital_Pin.pin1
  N2: U2.1IN-, Connector.3
  N3: U2.1IN+, R4.Pin_0
  N4: U2.VCC+, R1.Pin_0, LM317.OUT, R3.Pin_1, Connector.1
  N5: U2.VCC-, R2.Pin_1, INPUT.pin1, R4.Pin_1, Connector.2
  N6: R2.Pin_0, R1.Pin_1, LM317.ADJ
  N7: LM317.IN, INPUT.pin2
  N8: Buzzer.pin1, IC1.pin8
  N9: Buzzer.pin2, Switch.leg1
  N10: Switch.leg0, IC1.pin7
  N11: IC1.pin1, JP1.3
  N12: IC1.pin2, IC1.pin3, JP1.2
  N13: IC1.pin4, JP1.1
  GND: Contactor.COIL2, Part1.GND, Battery_2.-, Digital_Relay_Module.pin3, 12v_Regulator.GND, 5v_Regulator.GND, U3.GND, Brake_1.pin_1, Brake_2.pin_0, INPUT1.pin2, Sabertooth_2X60.pin5, Ultrasonic_Sensor_1.pin4
  N14: Contactor.NO, Sabertooth_2X60.pin1
  N15: Contactor.NC, Battery_1.+, Emergency_Stop_Switch_(NC).1, Brake_1.pin_0, Brake_2.pin_1, Switch_2.leg0
  N16: Contactor.COIL1, Digital_Relay_Module.pin5
  N17: Part1.D21/SCL, U3.DIN
  N18: Part1.D20/SDA, U3.DOUT
  N19: Part1.D13_PWM, To_Arduino_Digital_Pin1.pin2
  N20: Part1.D8_PWM, Digital_Relay_Module.pin2
  VIN: Part1.VIN, Digital_Relay_Module.pin1, 5v_Regulator.OUT, U3.VDD, Sabertooth_2X60.pin3, Ultrasonic_Sensor_1.pin1
  N21: Part1.D1/TX0, Sabertooth_2X60.pin4
  N22: Part1.D36, Ultrasonic_Sensor_1.pin2
  N23: Part1.D37, Ultrasonic_Sensor_1.pin3
  N24: Battery_1.-, Battery_2.+
  N25: Emergency_Stop_Switch_(NC).2, Digital_Relay_Module.pin6
  N26: 12v_Regulator.IN, 5v_Regulator.IN, Switch_2.leg1
  N27: 12v_Regulator.OUT, INPUT1.pin1
  N28: Motor_1.pin_1, Sabertooth_2X60.pin8
  N29: Motor_1.pin_2, Sabertooth_2X60.pin7
  N30: Motor_2.pin_1, Sabertooth_2X60.pin10
  N31: Motor_2.pin_2, Sabertooth_2X60.pin9
